# Fritzing sketch ondr (saved by Fritzing 0.8.7b)

parts:
  Součástka2 = Rotoshield - Motor driver shield for Arduino
  Součástka3 = Bluetooth HC-05 Macho
  M1 = DC Motor
  M2 = DC Motor
  Součástka1 = Arduino Uno (Rev3)  # not connected
  VCC1 = Battery
  M3 = DC Motor
  M4 = DC Motor

nets:
  N1: Součástka2.DIG_0, Součástka3.TXD
  N2: Součástka2.DIG_1, Součástka3.RXD
  GND: Součástka2.GND, Součástka3.GND, VCC1.-, M4.pin_1
  +5V: Součástka2.+5V, Součástka3.VCC
  N3: Součástka2.M1-2, M1.pin_2
  N4: Součástka2.M1-1, M1.pin_1
  N5: Součástka2.M2-2, M2.pin_2
  N6: Součástka2.M2-1, M2.pin_1
  N7: Součástka2.M3-2, M3.pin_2
  N8: Součástka2.M3-1, M3.pin_1
  N9: Součástka2.M4-1, M4.pin_2
  N10: Součástka2.VCC, VCC1.+
